// Logisim project hw4.circ as structural Verilog: 4 circuits, main circuit one-hot state machine
module one_hot_state_machine (
  input  CLK,
  input  ON,
  input  RST,
  output A,
  output B,
  output C,
  output D
);

  wire and_2_out, and_3_out, and_4_out, and_5_out, and_6_out, and_8_out, and_9_out, and_10_out, I0, I1, I2,
       I3, I4, I5, not_1_out, not_2_out, not_3_out, or_1_out, S0, S1, S2, S3, S4, S5;

  or or_1 (or_1_out, I0, I1, I2, I3, I4, I5);
  not not_1 (not_1_out, ON);
  and and_1 (S2, I1, ON);
  and and_2 (and_2_out, I0, not_2_out);
  not not_2 (not_2_out, ON);
  and and_3 (and_3_out, I3, ON);
  not not_3 (not_3_out, or_1_out);
  and and_4 (and_4_out, I2, not_1_out);
  or or_2 (S4, and_2_out, and_3_out);
  Register #(.width(6)) register_1 (
    .D({S5, S4, S3, S2, S1, S0}), .en(ON), .Q({I5, I4, I3, I2, I1, I0}), .clk(CLK), .clr(RST));
  or or_3 (S0, not_3_out, and_4_out);
  or or_4 (A, I0, I3, I5);
  or or_5 (C, I4, I2, I1);
  and and_5 (and_5_out, I0, ON);
  and and_6 (and_6_out, I5, ON);
  and and_7 (S3, I2, ON);
  and and_8 (and_8_out, I5, ~ON);  // AND_Gate
  and and_9 (and_9_out, I1, ~ON);  // AND_Gate
  and and_10 (and_10_out, I3, ~ON);  // AND_Gate
  or or_6 (S1, and_5_out, and_6_out);
  or or_7 (S5, and_8_out, and_9_out, and_10_out, I4);
  or or_8 (B, I2, I3);
  or or_9 (D, I5, I4, I3, I1);

  // Notes on the sheet:
  //   Do not place anything here!
  //   Moving the input and output pins of this subcircuit will break the tester subcircuit
endmodule

module reduced_state_machine (
  input  CLK,
  input  ON,
  input  RST,
  output A,
  output B,
  output C,
  output D
);

  wire and_1_out, and_2_out, and_3_out, and_4_out, and_5_out, and_6_out, and_7_out, and_8_out, and_9_out,
       and_10_out, and_11_out, and_12_out, and_13_out, I0, I2, S0, S1, S2;

  and and_1 (and_1_out, ~B, ~ON);  // AND_Gate
  and and_2 (and_2_out, I2, ~I0);  // AND_Gate
  or or_1 (S2, and_1_out, and_2_out, and_3_out);
  and and_3 (and_3_out, B, I0);
  Register #(.width(3)) register_1 (.D({S2, S1, S0}), .en(ON), .Q({I2, B, I0}), .clk(CLK), .clr(RST));
  and and_4 (and_4_out, I2, I0);
  and and_5 (and_5_out, I0, B);
  and and_6 (and_6_out, ~I0, ~B, ~I2);  // AND_Gate
  and and_7 (and_7_out, ~I2, ~B, I0, ON);  // AND_Gate
  or or_2 (S1, and_7_out, and_8_out);
  and and_8 (and_8_out, ~I0, B, ON);  // AND_Gate
  or or_3 (A, and_4_out, and_5_out, and_6_out);
  and and_9 (and_9_out, ON, ~I0);  // AND_Gate
  or or_4 (S0, and_9_out, I2, and_10_out);
  and and_10 (and_10_out, ~ON, I0);  // AND_Gate
  and and_11 (and_11_out, I0, ~B, ~I2);  // AND_Gate
  and and_12 (and_12_out, B, ~I0);  // AND_Gate
  or or_5 (C, and_11_out, and_12_out, and_13_out);
  and and_13 (and_13_out, I2, ~I0);  // AND_Gate
  or or_6 (D, I2, I0);

  // Other names for the same wires on the sheet: I1 = B

  // Notes on the sheet:
  //   Do not place anything here!
  //   Moving the input and output pins of this subcircuit will break the tester subcircuit
endmodule

module one_hot_checker (
);

  wire NEXT_out, one_hot_checker_1_p2, one_hot_state_machine_1_a, one_hot_state_machine_1_b,
       one_hot_state_machine_1_c, one_hot_state_machine_1_d, RESET_out;

  Clock NEXT (.out(NEXT_out));
  Button RESET (.out(RESET_out));
  // One_Hot_Checker one_hot_checker_1: pin names not known; wires that end beside it: RESET_out, one_hot_checker_1_p2
  one_hot_state_machine one_hot_state_machine_1 (
    .CLK(NEXT_out), .ON(one_hot_checker_1_p2), .RST(RESET_out), .A(one_hot_state_machine_1_a),
    .B(one_hot_state_machine_1_b), .C(one_hot_state_machine_1_c), .D(one_hot_state_machine_1_d));
endmodule

module reduced_checker (
);

  wire NEXT_out, reduced_checker_1_p2, reduced_state_machine_1_a, reduced_state_machine_1_b,
       reduced_state_machine_1_c, reduced_state_machine_1_d, RESET_out;

  Clock NEXT (.out(NEXT_out));
  Button RESET (.out(RESET_out));
  // Reduced_Checker reduced_checker_1: pin names not known; wires that end beside it: RESET_out, reduced_checker_1_p2
  reduced_state_machine reduced_state_machine_1 (
    .CLK(NEXT_out), .ON(reduced_checker_1_p2), .RST(RESET_out), .A(reduced_state_machine_1_a),
    .B(reduced_state_machine_1_b), .C(reduced_state_machine_1_c), .D(reduced_state_machine_1_d));
endmodule
